// Digital circuit ISA64C1024AL.dig as structural Verilog
module ISA64C1024AL (
  input  A0,
  input  A1,
  input  A2,
  input  A3,
  input  A4,
  input  A5,
  input  A6,
  input  A7,
  input  A8,
  input  A9,
  input  A10,
  input  A11,
  input  A12,
  input  A13,
  input  A14,
  input  A15,
  input  A16,
  input  VCC,
  input  GND,
  input  nCE1,
  input  nOE,
  input  nWE,
  input  CE2,
  output D0,
  output D1,
  output D2,
  output D3,
  output D4,
  output D5,
  output D6,
  output D7
);

  wire nand_1_out, nor_1_out;
  wire [7:0] ramsingleportsel_d;

  PowerSupply powersupply_1 (.VDD(VCC), .GND(GND));
  nand nand_1 (nand_1_out, ~nCE1, CE2);  // NAnd
  RAMSinglePortSel #(.AddrBits(17), .Bits(8)) ramsingleportsel (
    .A({A16, A15, A14, A13, A12, A11, A10, A9, A8, A7, A6, A5, A4, A3, A2, A1, A0}), .CS(~nand_1_out),
    .WE(~nWE), .OE(~nOE), .D(ramsingleportsel_d));
  nor nor_1 (nor_1_out, ~nWE, nand_1_out, nOE);  // NOr
  BusSplitter #(.Bits(8)) bussplitter_1 (
    .D(ramsingleportsel_d), .OE(nor_1_out), .D0(D0), .D1(D1), .D2(D2), .D3(D3), .D4(D4), .D5(D5), .D6(D6),
    .D7(D7));

  // Notes on the sheet:
  //   A0: pin 20
  //   A1: pin 19
  //   A2: pin 18
  //   A3: pin 17
  //   A4: pin 16
  //   A5: pin 15
  //   A6: pin 14
  //   A7: pin 13
  //   A8: pin 3
  //   A9: pin 2
  //   A10: pin 31
  //   A11: pin 1
  //   A12: pin 12
  //   A13: pin 4
  //   A14: pin 11
  //   A15: pin 7
  //   A16: pin 10
  //   D0: pin 21
  //   D1: pin 22
  //   D2: pin 23
  //   D3: pin 25
  //   D4: pin 26
  //   D5: pin 27
  //   D6: pin 28
  //   D7: pin 29
  //   VCC: pin 8, default 1
  //   GND: pin 24
  //   nCE1: pin 30, default 1
  //   nOE: pin 32, default 1
  //   nWE: pin 5, default 1
  //   CE2: pin 6, default 1
endmodule
