// Digital circuit clock.dig as structural Verilog
module clock (
  input  SW,
  input  STEP,
  input  [15:0] PC,
  input  HLT,
  input  eCLK,
  output CLK
);

  wire BRK_eq, d_ff_1_nq, d_ff_1_q, driverinvsel_1_out, HLT_t, multiplexer_1_out;

  not not_1 (HLT_t, HLT);
  Comparator #(.Bits(16)) BRK (.a(16'h1), .b(PC), .eq(BRK_eq));  // open: gt, lt
  assign driverinvsel_1_out = ~BRK_eq ? eCLK : 1'bz;  // DriverInvSel driverinvsel_1
  Multiplexer multiplexer_1 (.sel(d_ff_1_q), .in_0(driverinvsel_1_out), .in_1(STEP), .out(multiplexer_1_out));
  assign CLK = ~HLT_t ? multiplexer_1_out : 1'bz;  // DriverInvSel driverinvsel_2
  D_FF d_ff_1 (.D(d_ff_1_nq), .C(SW), .Q(d_ff_1_q), .nQ(d_ff_1_nq));
endmodule
