// Digital circuit sync.dig as structural Verilog
module sync (
  input  CLK,
  output nHSYNC,
  output nHBLANK,
  output [8:0] XPOS,
  output nVSYNC,
  output nVBLANK,
  output [9:0] YPOS,
  output nOE
);

  wire _74163_1_p12, _74163_1_p13, _74163_1_p14, _74163_1_p16, _74163_2_p16, _74163_4_p16, _74163_5_p16,
       _74163_7_p16, _74163_8_p16, _74377_1_p5, _74377_1_p6, _74377_1_p8, _74377_1_p9, _74377_1_p10,
       not_1_out, not_2_out, S3, S4, S5, S6, S7, S8, X_RST, Y_CNT, Y_RST;

  // Probe on {YPOS[8:0], S8, S7, S6, S5, S4, S3}
  // _74163 _74163_1: pin names not known; wires that end beside it: 1'b1, 1'b0, 1'b1, 1'b0, 1'b0, 1'b0, X_RST, CLK, 1'b1, 1'b1, 1'b1, _74163_1_p12, _74163_1_p13, _74163_1_p14, S3, _74163_1_p16, _74163_1_p12, _74163_1_p13, _74163_1_p14
  // _74163 _74163_2: pin names not known; wires that end beside it: 1'b1, 1'b0, 1'b0, 1'b0, 1'b0, 1'b0, 1'b1, CLK, 1'b1, _74163_1_p16, X_RST, S4, S5, S6, S7, _74163_2_p16
  // _74163 _74163_3: pin names not known; wires that end beside it: 1'b1, 1'b0, 1'b0, 1'b0, 1'b0, 1'b0, 1'b1, CLK, 1'b1, _74163_2_p16, X_RST, S8
  // _74163 _74163_4: pin names not known; wires that end beside it: 1'b1, 1'b0, 1'b0, 1'b0, 1'b0, 1'b0, 1'b1, CLK, 1'b1, 1'b1, X_RST, XPOS[0], XPOS[1], XPOS[2], XPOS[3], _74163_4_p16
  // _74163 _74163_5: pin names not known; wires that end beside it: 1'b1, 1'b0, 1'b0, 1'b0, 1'b0, 1'b0, 1'b1, CLK, 1'b1, _74163_4_p16, X_RST, XPOS[4], XPOS[5], XPOS[6], XPOS[7], _74163_5_p16
  // _74163 _74163_6: pin names not known; wires that end beside it: 1'b1, 1'b0, 1'b0, 1'b0, 1'b0, 1'b0, 1'b1, CLK, 1'b1, _74163_5_p16, X_RST, XPOS[8]
  FL_28c256 fl_28c256_1 (
    .A0(S3), .A1(S4), .A2(S5), .A3(S6), .A4(S7), .A5(S8), .A6(YPOS[0]), .A7(YPOS[1]), .A8(YPOS[2]),
    .A9(YPOS[3]), .A10(YPOS[4]), .A11(YPOS[5]), .A12(YPOS[6]), .A13(YPOS[7]), .A14(YPOS[8]), .A15(YPOS[9]),
    .nCE(1'b0), .nWE(1'b1), .nOE(1'b0), .VCC(1'b1), .GND(1'b0), .I_O0(X_RST), .I_O1(Y_RST),
    .I_O2(_74377_1_p5), .I_O3(_74377_1_p6), .I_O4(Y_CNT), .I_O5(_74377_1_p8), .I_O6(_74377_1_p9),
    .I_O7(_74377_1_p10));
  not not_1 (not_1_out, X_RST);
  not not_2 (not_2_out, X_RST);
  // _74163 _74163_7: pin names not known; wires that end beside it: 1'b1, 1'b0, 1'b0, 1'b0, 1'b0, 1'b0, 1'b1, CLK, Y_CNT, S8, Y_RST, YPOS[0], YPOS[1], YPOS[2], YPOS[3], _74163_7_p16
  // _74163 _74163_8: pin names not known; wires that end beside it: 1'b1, 1'b0, 1'b0, 1'b0, 1'b0, 1'b0, 1'b1, CLK, not_1_out, _74163_7_p16, Y_RST, YPOS[4], YPOS[5], YPOS[6], YPOS[7], _74163_8_p16
  // _74163 _74163_9: pin names not known; wires that end beside it: 1'b1, 1'b0, 1'b0, 1'b0, 1'b0, 1'b0, 1'b1, CLK, not_2_out, _74163_8_p16, Y_RST, YPOS[8], YPOS[9]
  // _74377 _74377_1: pin names not known; wires that end beside it: 1'b1, 1'b0, X_RST, Y_RST, _74377_1_p5, _74377_1_p6, Y_CNT, _74377_1_p8, _74377_1_p9, _74377_1_p10, 1'b0, CLK, nHSYNC, nVSYNC, nHBLANK, nVBLANK, nOE
  // Probe on XPOS

  // Other names for the same wires on the sheet: H0 = XPOS[0]; H1 = XPOS[1]; H2 = XPOS[2]; H3 = XPOS[3]; H4 = XPOS[4];
  //   H5 = XPOS[5]; H6 = XPOS[6]; H7 = XPOS[7]; H8 = XPOS[8]; OE = nOE; V0 = YPOS[0]; V1 = YPOS[1]; V2 = YPOS[2];
  //   V3 = YPOS[3]; V4 = YPOS[4]; V5 = YPOS[5]; V6 = YPOS[6]; V7 = YPOS[7]; V8 = YPOS[8]; V9 = YPOS[9]

  // Notes on the sheet:
  //   Clock Rate should be 12587500
  //   SYNC Counter
  //   Horizontal Counter
  //   Verticle Counter
  //   OUTPUTS
endmodule
