// Digital circuit tilegen.dig as structural Verilog
module tilegen (
  input  [17:0] iMB,
  input  [7:0] DB,
  input  nOE,
  input  LDM,
  input  LDA,
  input  LDT,
  input  NC,
  output [7:0] TPIXEL
);

  wire _7404_1_p9, _7404_1_p10, _7404_1_p11, _7404_1_p12, _7404_1_p13, _7404_1_p14, ATTR1_d6, ATTR1_d7,
       FLIPX, FLIPY;
  wire [3:0] Palette;
  wire [10:0] _74157_2_p15;
  wire [13:0] _74157_6_p13, FTILE;

  // _74157 _74157_1: pin names not known; wires that end beside it: iMB[3], iMB[4], iMB[5], iMB[6], iMB[0], iMB[1], iMB[2], iMB[3], nOE, 1'b0, 1'b1, 1'b0, _74157_2_p15[0], _74157_2_p15[1], _74157_2_p15[2], _74157_2_p15[3]
  // _74157 _74157_2: pin names not known; wires that end beside it: iMB[7], iMB[8], iMB[13], iMB[14], iMB[4], iMB[5], iMB[6], iMB[7], nOE, 1'b0, 1'b1, 1'b0, _74157_2_p15[4], _74157_2_p15[5], _74157_2_p15[6], _74157_2_p15[7]
  // _74157 _74157_3: pin names not known; wires that end beside it: iMB[15], iMB[16], iMB[17], 1'b0, iMB[8], iMB[9], iMB[10], iMB[11], nOE, 1'b0, 1'b1, 1'b0, _74157_2_p15[8], _74157_2_p15[9], _74157_2_p15[10]
  ISA64C1024AL MAP1 (
    .A0(_74157_2_p15[0]), .A1(_74157_2_p15[1]), .A2(_74157_2_p15[2]), .A3(_74157_2_p15[3]),
    .A4(_74157_2_p15[4]), .A5(_74157_2_p15[5]), .A6(_74157_2_p15[6]), .A7(_74157_2_p15[7]),
    .A8(_74157_2_p15[8]), .A9(_74157_2_p15[9]), .A10(_74157_2_p15[10]), .A11(1'b0), .A12(1'b0), .A13(1'b0),
    .A14(1'b0), .A15(1'b0), .A16(1'b0), .nCE1(1'b0), .CE2(1'b1), .nOE(nOE), .nWE(LDM), .VCC(1'b1),
    .GND(1'b0), .D0(FTILE[6]), .D1(FTILE[7]), .D2(FTILE[8]), .D3(FTILE[9]), .D4(FTILE[10]), .D5(FTILE[11]),
    .D6(FTILE[12]), .D7(FTILE[13]));
  ISA64C1024AL ATTR1 (
    .A0(_74157_2_p15[0]), .A1(_74157_2_p15[1]), .A2(_74157_2_p15[2]), .A3(_74157_2_p15[3]),
    .A4(_74157_2_p15[4]), .A5(_74157_2_p15[5]), .A6(_74157_2_p15[6]), .A7(_74157_2_p15[7]),
    .A8(_74157_2_p15[8]), .A9(_74157_2_p15[9]), .A10(_74157_2_p15[10]), .A11(1'b0), .A12(1'b0), .A13(1'b0),
    .A14(1'b0), .A15(1'b0), .A16(1'b0), .nCE1(1'b0), .CE2(1'b1), .nOE(nOE), .nWE(LDA), .VCC(1'b1),
    .GND(1'b0), .D0(FLIPX), .D1(FLIPY), .D2(Palette[0]), .D3(Palette[1]), .D4(Palette[2]), .D5(Palette[3]),
    .D6(ATTR1_d6), .D7(ATTR1_d7));
  // _74245 _74245_1: pin names not known; wires that end beside it: DB[7], DB[6], FTILE[13], DB[5], FTILE[12], DB[4], FTILE[11], DB[3], FTILE[10], DB[2], FTILE[9], DB[1], FTILE[8], DB[0], FTILE[7], 1'b0, FTILE[6], 1'b1, LDM, 1'b1
  // _74245 _74245_2: pin names not known; wires that end beside it: DB[7], DB[6], ATTR1_d7, DB[5], ATTR1_d6, DB[4], Palette[3], DB[3], Palette[2], DB[2], Palette[1], DB[1], Palette[0], DB[0], FLIPY, 1'b0, FLIPX, 1'b1, LDA, 1'b1
  // _7404 _7404_1: pin names not known; wires that end beside it: iMB[0], iMB[1], iMB[2], iMB[10], iMB[11], iMB[12], 1'b1, 1'b0, _7404_1_p9, _7404_1_p10, _7404_1_p11, _7404_1_p12, _7404_1_p13, _7404_1_p14
  // _74157 _74157_4: pin names not known; wires that end beside it: iMB[0], iMB[1], iMB[2], 1'b0, _7404_1_p9, _7404_1_p10, _7404_1_p11, 1'b0, FLIPX, 1'b0, 1'b1, 1'b0, FTILE[0], FTILE[1], FTILE[2]
  // _74157 _74157_5: pin names not known; wires that end beside it: iMB[10], iMB[11], iMB[12], 1'b0, _7404_1_p12, _7404_1_p13, _7404_1_p14, 1'b0, FLIPY, 1'b0, 1'b1, 1'b0, FTILE[3], FTILE[4], FTILE[5]
  // _74157 _74157_6: pin names not known; wires that end beside it: FTILE[0], FTILE[1], FTILE[2], FTILE[3], iMB[0], iMB[1], iMB[2], iMB[3], nOE, 1'b0, 1'b1, 1'b0, _74157_6_p13[0], _74157_6_p13[1], _74157_6_p13[2], _74157_6_p13[3]
  // _74157 _74157_7: pin names not known; wires that end beside it: FTILE[4], FTILE[5], FTILE[6], FTILE[7], iMB[4], iMB[5], iMB[6], iMB[7], nOE, 1'b0, 1'b1, 1'b0, _74157_6_p13[4], _74157_6_p13[5], _74157_6_p13[6], _74157_6_p13[7]
  // _74157 _74157_8: pin names not known; wires that end beside it: FTILE[8], FTILE[9], FTILE[10], FTILE[11], iMB[8], iMB[9], iMB[10], iMB[11], nOE, 1'b0, 1'b1, 1'b0, _74157_6_p13[8], _74157_6_p13[9], _74157_6_p13[10], _74157_6_p13[11]
  // _74157 _74157_9: pin names not known; wires that end beside it: FTILE[12], FTILE[13], 1'b0, 1'b0, iMB[12], iMB[14], 1'b0, 1'b0, nOE, 1'b0, 1'b1, 1'b0, _74157_6_p13[12], _74157_6_p13[13]
  ISA64C1024AL TILE_CACHE (
    .A0(_74157_6_p13[0]), .A1(_74157_6_p13[1]), .A2(_74157_6_p13[2]), .A3(_74157_6_p13[3]),
    .A4(_74157_6_p13[4]), .A5(_74157_6_p13[5]), .A6(_74157_6_p13[6]), .A7(_74157_6_p13[7]),
    .A8(_74157_6_p13[8]), .A9(_74157_6_p13[9]), .A10(_74157_6_p13[10]), .A11(_74157_6_p13[11]),
    .A12(_74157_6_p13[12]), .A13(_74157_6_p13[13]), .A14(1'b0), .A15(1'b0), .A16(1'b0), .nCE1(1'b0),
    .CE2(1'b1), .nOE(nOE), .nWE(LDT), .VCC(1'b1), .GND(1'b0), .D0(TPIXEL[0]), .D1(TPIXEL[1]), .D2(TPIXEL[2]),
    .D3(TPIXEL[3]), .D4(TPIXEL[4]), .D5(TPIXEL[5]), .D6(TPIXEL[6]), .D7(TPIXEL[7]));
  // _74245 _74245_3: pin names not known; wires that end beside it: DB[7], DB[6], TPIXEL[7], DB[5], TPIXEL[6], DB[4], TPIXEL[5], DB[3], TPIXEL[4], DB[2], TPIXEL[3], DB[1], TPIXEL[2], DB[0], TPIXEL[1], 1'b0, TPIXEL[0], 1'b1, LDT, 1'b1

  // Other names for the same wires on the sheet: TILE_ID[7:0] = FTILE[13:6]; PIXEL_X[2:0] = FTILE[2:0];
  //   PIXEL_Y[2:0] = FTILE[5:3]; PRE_PIXEL[7:0] = TPIXEL; X[8:0] = iMB[8:0]; Xi[2:0] = iMB[2:0]; XY[17:0] = iMB;
  //   TILE_ADDR[10:0] = {iMB[17:13], iMB[8:3]}; Y[7:0] = iMB[17:10]; Yi[2:0] = iMB[12:10]

  // Notes on the sheet:
  //   LDM: default 1
  //   LDA: default 1
  //   LDT: default 1
  //   STAGE 1: Decode Tile ID and Attr
  //   INPUT
  //   XY - 18 bits from CPU [ 8Y9X ]
  //   DB -   8 bits from CPU
  //   OE - Output Enable
  //   WE - Write Enable
  //   LDM - Load Map Data
  //   LDA - Load Attribute Data
  //   LDT - Load TileCache Data
  //   CLK - 12Mhz GPU Clock
  //   Bus Splits
  //   STAGE 2: Generate exact pixel address
  //   TILE-ADDR is an 11 bit address. YYYYY-XXXXXX
  //   X and Y are /8 to generate tile address
  //   Xi and Yi (index value) are the exact pixel location
  //   inside the tile to render. 3 LSB of X and Y
  //   FTILE is the full tile cache address
  //   PIXEL-X and Y are the normal or inverted index
  //   locations for the pixel being rendered
  //   STAGE 3: Get pixel color index
  //   OUTPUT
endmodule
